// Logisim project part2c.circ as structural Verilog: 3 circuits, main circuit main
// FunSel
module main (
  input  [7:0] A,
  input  [7:0] B,
  input  [3:0] FunSel,
  output [7:0] out_4
);

  wire clock_1_out, multiplexer_1_out, multiplexer_6_out, multiplexer_12_out, multiplexer_14_out, nand_1_out,
       not_3_out, or_2_out;
  wire [3:0] C_q, nor_1_out;
  wire [7:0] adder_1_out, and_1_out, multiplexer_3_out, multiplexer_11_out, not_1_out, not_2_out, or_1_out,
       xor_1_out;

  assign not_1_out = ~A;  // NOT_Gate not_1, 8 bits wide
  Multiplexer #(.select(2), .enable("false")) multiplexer_1 (
    .in0(1'b0), .in1(1'b0), .in2(A[7]), .in3(C_q[1]), .out(multiplexer_1_out), .sel(FunSel[2:1]));
  assign not_2_out = ~B;  // NOT_Gate not_2, 8 bits wide
  Multiplexer #(.enable("false")) multiplexer_2 (
    .in0(A[6]), .in1(multiplexer_1_out), .out(multiplexer_11_out[7]), .sel(FunSel[0]));
  Multiplexer #(.width(8), .enable("false")) multiplexer_3 (
    .in0(B), .in1(not_2_out), .out(multiplexer_3_out), .sel(FunSel[1]));
  Multiplexer #(.enable("false")) multiplexer_4 (.in0(A[5]), .in1(A[7]), .out(multiplexer_11_out[6]), .sel(FunSel[0]));
  Adder adder_1 (.a(A), .b(multiplexer_3_out), .out(adder_1_out), .cin(multiplexer_6_out), .cout(nor_1_out[1]));
  Multiplexer #(.enable("false")) multiplexer_5 (.in0(A[4]), .in1(A[6]), .out(multiplexer_11_out[5]), .sel(FunSel[0]));
  Multiplexer #(.enable("false")) multiplexer_6 (
    .in0(or_2_out), .in1(C_q[1]), .out(multiplexer_6_out), .sel(FunSel[0]));
  assign and_1_out = A & B;  // AND_Gate and_1, 8 bits wide
  assign or_1_out = A | B;  // OR_Gate or_1, 8 bits wide
  assign xor_1_out = A ^ B;  // XOR_Gate xor_1, 8 bits wide
  Multiplexer #(.enable("false")) multiplexer_7 (.in0(A[2]), .in1(A[4]), .out(multiplexer_11_out[3]), .sel(FunSel[0]));
  Multiplexer #(.enable("false")) multiplexer_8 (.in0(A[3]), .in1(A[5]), .out(multiplexer_11_out[4]), .sel(FunSel[0]));
  or or_2 (or_2_out, FunSel[0], FunSel[1]);
  Multiplexer #(.enable("false")) multiplexer_9 (.in0(A[1]), .in1(A[3]), .out(multiplexer_11_out[2]), .sel(FunSel[0]));
  Multiplexer #(.enable("false")) multiplexer_10 (.in0(A[0]), .in1(A[2]), .out(multiplexer_11_out[1]), .sel(FunSel[0]));
  Multiplexer #(.enable("false")) multiplexer_11 (
    .in0(multiplexer_12_out), .in1(A[1]), .out(multiplexer_11_out[0]), .sel(FunSel[0]));
  Multiplexer #(.select(2), .enable("false")) multiplexer_12 (
    .in0(1'b0), .in1(1'b0), .in2(1'b0), .in3(C_q[1]), .out(multiplexer_12_out), .sel(FunSel[2:1]));
  Multiplexer #(.select(4), .width(8), .enable("false")) multiplexer_13 (
    .in0(A), .in1(B), .in2(not_1_out), .in3(not_2_out), .in4(adder_1_out), .in5(adder_1_out),
    .in6(adder_1_out), .in7(and_1_out), .in8(or_1_out), .in9(xor_1_out), .in10(multiplexer_11_out),
    .in11(multiplexer_11_out), .in12(multiplexer_11_out), .in13(multiplexer_11_out),
    .in14(multiplexer_11_out), .in15(multiplexer_11_out), .out(out_4), .sel(FunSel));
  not not_3 (not_3_out, FunSel[1]);
  Multiplexer #(.enable("false")) multiplexer_14 (.in0(A[7]), .in1(A[0]), .out(multiplexer_14_out), .sel(FunSel[0]));
  nor nor_1 (nor_1_out[0], out_4[0], out_4[1], out_4[2], out_4[3], out_4[4], out_4[5], out_4[6], out_4[7]);
  nand nand_1 (nand_1_out, FunSel[0], not_3_out, FunSel[2], FunSel[3]);
  and and_2 (nor_1_out[2], out_4[7], nand_1_out);
  Clock clock_1 (.out(clock_1_out));
  Register #(.width(4)) C (.D(nor_1_out), .en(1'b1), .Q(C_q), .clk(clock_1_out));  // open: clr
endmodule

module Register16 (
  input  in_1,
  input  E,
  input  [15:0] I,
  input  [1:0] FunSel,
  output [15:0] out_5
);

  wire not_2_out;
  wire [15:0] adder_1_out, multiplexer_1_out, multiplexer_2_out, multiplexer_3_out, not_1_out;

  Multiplexer #(.width(16), .enable("false")) multiplexer_1 (
    .in0(16'h1), .in1(not_1_out), .out(multiplexer_1_out), .sel(not_2_out));
  assign not_1_out = ~16'h1;  // NOT_Gate not_1, 16 bits wide
  Multiplexer #(.width(16), .enable("false")) multiplexer_2 (
    .in0(I), .in1({16{1'b0}}), .out(multiplexer_2_out), .sel(FunSel[0]));
  Adder #(.width(16)) adder_1 (.a(out_5), .b(multiplexer_1_out), .out(adder_1_out), .cin(not_2_out));  // open: cout
  not not_2 (not_2_out, FunSel[0]);
  D_Flip_Flop d_ff_1 (.clk(in_1), .D(multiplexer_3_out[15]), .Q(out_5[15]), .en(E));  // open: Qn, preset, reset
  Multiplexer #(.width(16), .enable("false")) multiplexer_3 (
    .in0(adder_1_out), .in1(multiplexer_2_out), .out(multiplexer_3_out), .sel(FunSel[1]));
  D_Flip_Flop d_ff_2 (.clk(in_1), .D(multiplexer_3_out[14]), .Q(out_5[14]), .en(E));  // open: Qn, preset, reset
  D_Flip_Flop d_ff_3 (.clk(in_1), .D(multiplexer_3_out[13]), .Q(out_5[13]), .en(E));  // open: Qn, preset, reset
  D_Flip_Flop d_ff_4 (.clk(in_1), .D(multiplexer_3_out[12]), .Q(out_5[12]), .en(E));  // open: Qn, preset, reset
  D_Flip_Flop d_ff_5 (.clk(in_1), .D(multiplexer_3_out[11]), .Q(out_5[11]), .en(E));  // open: Qn, preset, reset
  D_Flip_Flop d_ff_6 (.clk(in_1), .D(multiplexer_3_out[10]), .Q(out_5[10]), .en(E));  // open: Qn, preset, reset
  D_Flip_Flop d_ff_7 (.clk(in_1), .D(multiplexer_3_out[9]), .Q(out_5[9]), .en(E));  // open: Qn, preset, reset
  D_Flip_Flop d_ff_8 (.clk(in_1), .D(multiplexer_3_out[8]), .Q(out_5[8]), .en(E));  // open: Qn, preset, reset
  D_Flip_Flop d_ff_9 (.clk(in_1), .D(multiplexer_3_out[7]), .Q(out_5[7]));  // open: Qn, preset, en, reset
  D_Flip_Flop d_ff_10 (.clk(in_1), .D(multiplexer_3_out[6]), .Q(out_5[6]));  // open: Qn, preset, en, reset
  D_Flip_Flop d_ff_11 (.clk(in_1), .D(multiplexer_3_out[5]), .Q(out_5[5]), .en(E));  // open: Qn, preset, reset
  D_Flip_Flop d_ff_12 (.clk(in_1), .D(multiplexer_3_out[4]), .Q(out_5[4]), .en(E));  // open: Qn, preset, reset
  D_Flip_Flop d_ff_13 (.clk(in_1), .D(multiplexer_3_out[3]), .Q(out_5[3]), .en(E));  // open: Qn, preset, reset
  D_Flip_Flop d_ff_14 (.clk(in_1), .D(multiplexer_3_out[2]), .Q(out_5[2]), .en(E));  // open: Qn, preset, reset
  D_Flip_Flop d_ff_15 (.clk(in_1), .D(multiplexer_3_out[1]), .Q(out_5[1]), .en(E));  // open: Qn, preset, reset
  D_Flip_Flop d_ff_16 (.clk(in_1), .D(multiplexer_3_out[0]), .Q(out_5[0]), .en(E));  // open: Qn, preset, reset
endmodule

module Shifter (
);

  wire clock_1_out, multiplexer_1_out, multiplexer_2_out, multiplexer_3_out, multiplexer_4_out,
       multiplexer_5_out, multiplexer_6_out, multiplexer_7_out, multiplexer_8_out, multiplexer_9_out,
       multiplexer_10_out, undriven_2, undriven_3, undriven_4, xor_1_out;
  wire [1:0] undriven;
  wire [7:0] d_ff_8_q;

  Multiplexer #(.select(2), .enable("false")) multiplexer_1 (
    .in0(1'b0), .in1(1'b0), .in2(d_ff_8_q[7]), .in3(d_ff_8_q[0]), .out(multiplexer_1_out), .sel(undriven));
  Clock clock_1 (.out(clock_1_out));
  Multiplexer #(.enable("false")) multiplexer_2 (
    .in0(d_ff_8_q[6]), .in1(multiplexer_1_out), .out(multiplexer_2_out), .sel(undriven_2));
  D_Flip_Flop d_ff_1 (.clk(clock_1_out), .D(multiplexer_2_out), .Q(d_ff_8_q[7]), .en(1'b1));  // open: Qn, preset, reset
  Multiplexer #(.enable("false")) multiplexer_3 (
    .in0(d_ff_8_q[5]), .in1(d_ff_8_q[7]), .out(multiplexer_3_out), .sel(undriven_2));
  D_Flip_Flop d_ff_2 (.clk(clock_1_out), .D(multiplexer_3_out), .Q(d_ff_8_q[6]), .en(1'b1));  // open: Qn, preset, reset
  Multiplexer #(.enable("false")) multiplexer_4 (
    .in0(d_ff_8_q[4]), .in1(d_ff_8_q[6]), .out(multiplexer_4_out), .sel(undriven_2));
  D_Flip_Flop d_ff_3 (.clk(clock_1_out), .D(multiplexer_4_out), .Q(d_ff_8_q[5]), .en(1'b1));  // open: Qn, preset, reset
  Multiplexer #(.enable("false")) multiplexer_5 (
    .in0(d_ff_8_q[3]), .in1(d_ff_8_q[5]), .out(multiplexer_5_out), .sel(undriven_2));
  D_Flip_Flop d_ff_4 (.clk(clock_1_out), .D(multiplexer_5_out), .Q(d_ff_8_q[4]), .en(1'b1));  // open: Qn, preset, reset
  Multiplexer #(.enable("false")) multiplexer_6 (
    .in0(d_ff_8_q[2]), .in1(d_ff_8_q[4]), .out(multiplexer_6_out), .sel(undriven_2));
  D_Flip_Flop d_ff_5 (.clk(clock_1_out), .D(multiplexer_6_out), .Q(d_ff_8_q[3]), .en(1'b1));  // open: Qn, preset, reset
  Multiplexer #(.enable("false")) multiplexer_7 (
    .in0(d_ff_8_q[1]), .in1(d_ff_8_q[3]), .out(multiplexer_7_out), .sel(undriven_2));
  D_Flip_Flop d_ff_6 (.clk(clock_1_out), .D(multiplexer_7_out), .Q(d_ff_8_q[2]), .en(1'b1));  // open: Qn, preset, reset
  Multiplexer #(.enable("false")) multiplexer_8 (
    .in0(d_ff_8_q[0]), .in1(d_ff_8_q[2]), .out(multiplexer_8_out), .sel(undriven_2));
  xor xor_1 (xor_1_out, undriven_4, undriven_3);
  D_Flip_Flop d_ff_7 (.clk(clock_1_out), .D(multiplexer_8_out), .Q(d_ff_8_q[1]), .en(1'b1));  // open: Qn, preset, reset
  Multiplexer #(.enable("false")) multiplexer_9 (
    .in0(d_ff_8_q[7]), .in1(1'b0), .out(multiplexer_9_out), .sel(xor_1_out));
  Multiplexer #(.enable("false")) multiplexer_10 (
    .in0(multiplexer_9_out), .in1(d_ff_8_q[1]), .out(multiplexer_10_out), .sel(undriven_2));
  D_Flip_Flop d_ff_8 (
    .clk(clock_1_out), .D(multiplexer_10_out), .Q(d_ff_8_q[0]), .en(1'b1));  // open: Qn, preset, reset
endmodule
